# Fritzing sketch barndoor (saved by Fritzing 0.7.4b)
breadboards: 2

parts:
  C1 = Tantalum Capacitor [capacitance="1 μF" package="100 mil [THT, tantalum]"]
  C2 = Tantalum Capacitor [capacitance="1 μF" package="100 mil [THT, tantalum]"]
  J1 = female pin header, 2 pins [form="♀ (female)"]
  U1 = Voltage Regulator - 5V [package="TO220 [THT]"]
  J2 = female pin header, 2 pins [form="♀ (female)"]
  D1 = Rectifier Diode [part_number=1N4001 package="300 mil [THT]"]
  IC1 = L293D [package=THT]
  XTAL1 = CRYSTAL - kHz [frequency="16 Mhz"]
  U2 = atmega328 [package=dip]
  Power = Power plug
  R1 = Resistor [tolerance=±5% resistance=220 package=THT]
  LED1 = LED - 3mm [color="Red (633nm)" package="3 mm [THT]"]

nets:
  GND: C1.-, C2.-, U1.GND, IC1.0V, U2.GND#21, Power.GND, LED1.anode
  N1: C1.+, U1.output_voltage, IC1.Enable_1, IC1.Enable_2, IC1.+V, U2.VCC
  N2: C2.+, U1.input_voltage, D1.cathode, IC1.+Vmotor, R1.Pin_0
  N3: J1.pin1, IC1.Out_3_(_Controlled_by_Enable_2_)
  N4: J1.pin2, IC1.Out_4_(_Controlled_by_Enable_2_)
  N5: J2.pin1, IC1.Out_2_(_Controlled_by_Enable_1_)
  N6: J2.pin2, IC1.Out_1_(_Controlled_by_Enable_1_)
  N7: D1.anode, Power.VCC
  N8: IC1.In_1, U2.D3_(PWM)
  N9: IC1.In_2, U2.D2
  N10: IC1.In_3, U2.D6_(PWM)
  N11: IC1.In_4, U2.D5_(PWM)
  N12: XTAL1.pin_0, U2.XLAT2
  N13: XTAL1.pin_1, U2.XLAT1
  N14: R1.Pin_1, LED1.cathode
